// Logisim project Koushik-Banerjee_1812171642.circ as structural Verilog
module NAND (
  input  _1,
  input  _2,
  input  _4,
  input  _5,
  input  _9,
  input  _10,
  input  _12,
  input  _13,
  output _3,
  output _6,
  output _8,
  output _11
);

  nand nand_1 (_3, _1, _2);
  nand nand_2 (_6, _4, _5);
  nand nand_3 (_8, _9, _10);
  nand nand_4 (_11, _12, _13);
endmodule

module AND (
  input  _1,
  input  _2,
  input  _4,
  input  _5,
  input  _9,
  input  _10,
  input  _12,
  input  _13,
  output _3,
  output _6,
  output _8,
  output _11
);

  and and_1 (_3, _1, _2);
  and and_2 (_6, _4, _5);
  and and_3 (_8, _9, _10);
  and and_4 (_11, _12, _13);
endmodule

module NOT (
  input  _1,
  input  _3,
  input  _5,
  input  _9,
  input  _11,
  input  _13,
  output _2,
  output _4,
  output _6,
  output _8,
  output _10,
  output _12
);

  not not_1 (_2, _1);
  not not_2 (_4, _3);
  not not_3 (_6, _5);
  not not_4 (_8, _9);
  not not_5 (_10, _11);
  not not_6 (_12, _13);
endmodule

module _2_input_OR (
  input  _1,
  input  _2,
  input  _4,
  input  _5,
  input  _9,
  input  _10,
  input  _12,
  input  _13,
  output _3,
  output _6,
  output _8,
  output _11
);

  or or_1 (_3, _1, _2);
  or or_2 (_6, _4, _5);
  or or_3 (_8, _9, _10);
  or or_4 (_11, _12, _13);
endmodule

module _3_input_OR (
  input  _14,
  input  _1,
  input  _2,
  input  _8,
  input  _3,
  input  _4,
  input  _5,
  input  _11,
  input  _12,
  input  _13,
  input  _7,
  output _9,
  output _6,
  output _10
);

  wire or_1_out, or_2_out, or_3_out;

  or or_1 (or_1_out, _1, _2);
  or or_2 (or_2_out, _3, _4);
  or or_3 (or_3_out, _11, _12);
  or or_4 (_9, or_1_out, _8);
  or or_5 (_6, or_2_out, _5);
  or or_6 (_10, or_3_out, _13);
endmodule

module _3_input_AND (
  input  _14,
  input  _1,
  input  _2,
  input  _13,
  input  _3,
  input  _4,
  input  _5,
  input  _9,
  input  _10,
  input  _11,
  input  _7,
  output _12,
  output _6,
  output _8
);

  wire and_1_out, and_2_out, and_3_out;

  and and_1 (and_1_out, _1, _2);
  and and_2 (and_2_out, _3, _4);
  and and_3 (and_3_out, _9, _10);
  and and_4 (_12, and_1_out, _13);
  and and_5 (_6, and_2_out, _5);
  and and_6 (_8, and_3_out, _11);
endmodule

module _7483_IC (
  input  C_in,
  input  B4,
  input  B3,
  input  B2,
  input  B1,
  input  A4,
  input  A3,
  input  A2,
  input  A1,
  output C_out,
  output S4,
  output S3,
  output S2,
  output S1
);

  wire and_1_out, and_2_out, and_3_out, and_4_out, and_5_out, and_6_out, and_7_out, and_8_out, or_1_out,
       or_2_out, or_3_out, xor_1_out, xor_2_out, xor_3_out, xor_4_out;

  xor xor_1 (xor_1_out, A1, B1);
  and and_1 (and_1_out, A1, B1);
  xor xor_2 (xor_2_out, A2, B2);
  and and_2 (and_2_out, A2, B2);
  xor xor_3 (xor_3_out, A3, B3);
  and and_3 (and_3_out, A3, B3);
  xor xor_4 (xor_4_out, A4, B4);
  and and_4 (and_4_out, A4, B4);
  and and_5 (and_5_out, xor_1_out, C_in);
  xor xor_5 (S1, xor_1_out, C_in);
  xor xor_6 (S2, xor_2_out, or_1_out);
  and and_6 (and_6_out, xor_2_out, or_1_out);
  xor xor_7 (S3, xor_3_out, or_3_out);
  and and_7 (and_7_out, xor_3_out, or_3_out);
  xor xor_8 (S4, xor_4_out, or_2_out);
  and and_8 (and_8_out, xor_4_out, or_2_out);
  or or_1 (or_1_out, and_5_out, and_1_out);
  or or_2 (or_2_out, and_7_out, and_3_out);
  or or_3 (or_3_out, and_6_out, and_2_out);
  or or_4 (C_out, and_8_out, and_4_out);
endmodule

module JK_flip_flop_IC (
  input  J,
  input  Preset,
  input  K,
  input  Clear,
  input  Clock,
  output Q,
  output Q_prime
);

  wire and_1_out, and_2_out, and_3_out, and_4_out, nor_1_out, nor_2_out, not_1_out, or_1_out, or_2_out;

  or or_1 (or_1_out, J, Preset);
  or or_2 (or_2_out, Preset, K);
  and and_1 (and_1_out, Q_prime, or_1_out, Clock);
  and and_2 (and_2_out, Clock, or_2_out, Q);
  not not_1 (not_1_out, Clock);
  nor nor_1 (nor_1_out, and_1_out, nor_2_out);
  nor nor_2 (nor_2_out, nor_1_out, and_2_out, Clear);
  and and_3 (and_3_out, not_1_out, nor_1_out);
  nor nor_3 (Q, and_3_out, Q_prime);
  and and_4 (and_4_out, nor_2_out, not_1_out);
  nor nor_4 (Q_prime, Q, and_4_out);
endmodule

module D_flip_flop_IC (
  input  D,
  input  CLOCK,
  input  in_3,
  input  in_4,
  output out_5,
  output out_6
);

  wire not_1_out;

  not not_1 (not_1_out, D);
  JK_flip_flop_IC jk_flip_flop_ic_1 (
    .J(D), .Preset(in_3), .K(not_1_out), .Q(out_5), .Q_prime(out_6), .Clock(CLOCK), .Clear(in_4));
endmodule

module p1 (
  input  in_1,
  input  in_2,
  input  in_3,
  output out_4,
  output out_5,
  output out_6
);

  wire and_1_out, and_2_out, and_3_out, and_4_out, and_5_out, d_flip_flop_ic_1_out_6, d_flip_flop_ic_2_out_6,
       d_flip_flop_ic_3_out_6, not_1_out, not_2_out, not_3_out, or_1_out, or_2_out;

  and and_1 (and_1_out, not_1_out, d_flip_flop_ic_2_out_6);
  and and_2 (and_2_out, d_flip_flop_ic_1_out_6, not_3_out, not_2_out);
  and and_3 (and_3_out, not_1_out, d_flip_flop_ic_3_out_6);
  and and_4 (and_4_out, d_flip_flop_ic_2_out_6, not_2_out);
  and and_5 (and_5_out, not_3_out, d_flip_flop_ic_3_out_6);
  or or_1 (or_1_out, and_1_out, and_2_out, and_3_out);
  not not_1 (not_1_out, d_flip_flop_ic_1_out_6);
  or or_2 (or_2_out, and_4_out, and_5_out);
  not not_2 (not_2_out, d_flip_flop_ic_3_out_6);
  D_flip_flop_IC d_flip_flop_ic_1 (
    .D(or_1_out), .out_5(out_4), .out_6(d_flip_flop_ic_1_out_6), .in_4(in_2), .in_3(in_1), .CLOCK(in_3));
  not not_3 (not_3_out, d_flip_flop_ic_2_out_6);
  D_flip_flop_IC d_flip_flop_ic_2 (
    .D(or_2_out), .out_5(out_5), .out_6(d_flip_flop_ic_2_out_6), .in_4(in_2), .in_3(in_1), .CLOCK(in_3));
  D_flip_flop_IC d_flip_flop_ic_3 (
    .D(d_flip_flop_ic_3_out_6), .out_5(out_6), .out_6(d_flip_flop_ic_3_out_6), .in_4(in_2), .in_3(in_1),
    .CLOCK(in_3));
endmodule

module _7_Segment_Basic_Gate (
  input  A,
  input  B,
  input  C
);

  wire and_1_out, and_2_out, and_3_out, and_4_out, and_5_out, and_6_out, and_7_out, and_8_out, and_9_out,
       and_10_out, and_11_out, and_12_out, and_13_out, and_14_out, not_1_out, not_2_out, not_3_out, or_1_out,
       or_2_out, or_3_out, or_4_out, or_5_out, or_6_out, or_7_out;

  not not_1 (not_1_out, A);
  not not_2 (not_2_out, B);
  not not_3 (not_3_out, C);
  and and_1 (and_1_out, not_1_out, C);
  and and_2 (and_2_out, A, not_3_out);
  and and_3 (and_3_out, B, not_3_out);
  and and_4 (and_4_out, A, not_2_out, C);
  and and_5 (and_5_out, not_1_out, B, not_3_out);
  and and_6 (and_6_out, not_1_out, C);
  and and_7 (and_7_out, B, not_3_out);
  and and_8 (and_8_out, A, not_2_out, not_3_out);
  and and_9 (and_9_out, not_1_out, C);
  and and_10 (and_10_out, B, C);
  and and_11 (and_11_out, not_1_out, B);
  and and_12 (and_12_out, not_1_out, C);
  and and_13 (and_13_out, A, not_3_out);
  and and_14 (and_14_out, A, not_2_out, not_3_out);
  or or_1 (or_1_out, and_1_out, and_2_out);
  or or_2 (or_2_out, and_3_out, and_4_out, and_5_out);
  or or_3 (or_3_out, A, not_3_out);
  or or_4 (or_4_out, and_6_out, and_7_out, and_8_out);
  or or_5 (or_5_out, and_12_out, and_13_out);
  or or_6 (or_6_out, B, and_14_out);
  or or_7 (or_7_out, and_9_out, and_10_out, and_11_out);
  _7_Segment_Display u_7_segment_display_1 (
    .g(or_6_out), .f(or_5_out), .a(or_1_out), .b(or_2_out), .e(or_7_out), .d(or_4_out), .c(or_3_out));  // open: dp
endmodule

module _7_Segment_Universal (
  input  A,
  input  B,
  input  C,
  output out_4,
  output out_5,
  output out_6,
  output out_7,
  output out_8,
  output out_9,
  output out_10
);

  wire nand_1_out, nand_2_out, nand_3_out, nand_4_out, nand_5_out, nand_6_out, nand_7_out, nand_8_out,
       nand_9_out, nand_10_out, nand_11_out, nand_12_out, nand_13_out, nand_14_out, nand_15_out, nand_16_out,
       nand_17_out, nand_18_out, nand_19_out, nand_20_out, nand_21_out, nand_22_out, nand_23_out,
       nand_24_out, nand_25_out, nand_26_out, nand_27_out, nand_28_out, nand_29_out, nand_30_out,
       nand_31_out, nand_32_out, nand_33_out, nand_34_out, nand_35_out, nand_36_out, nand_37_out,
       nand_38_out, nand_39_out, nand_40_out, nand_41_out, nand_42_out, nand_43_out, nand_44_out,
       nand_45_out, not_1_out, not_2_out, not_3_out;

  not not_1 (not_1_out, A);
  not not_2 (not_2_out, B);
  not not_3 (not_3_out, C);
  nand nand_1 (nand_1_out, not_1_out, C);
  nand nand_2 (nand_2_out, not_1_out, C);
  nand nand_3 (nand_3_out, B, not_3_out);
  nand nand_4 (nand_4_out, A, not_2_out, not_3_out);
  nand nand_5 (nand_5_out, not_1_out, C);
  nand nand_6 (nand_6_out, B, C);
  nand nand_7 (nand_7_out, not_1_out, B);
  nand nand_8 (nand_8_out, A, not_3_out);
  nand nand_9 (nand_9_out, nand_1_out, nand_1_out);
  nand nand_10 (nand_10_out, A, not_3_out);
  nand nand_11 (nand_11_out, not_2_out, not_3_out);
  nand nand_12 (nand_12_out, A, not_2_out, C);
  nand nand_13 (nand_13_out, not_1_out, B, not_3_out);
  nand nand_14 (nand_14_out, not_1_out, C);
  nand nand_15 (nand_15_out, nand_8_out, nand_8_out);
  nand nand_16 (nand_16_out, A, not_2_out, not_3_out);
  nand nand_17 (nand_17_out, nand_10_out, nand_10_out);
  nand nand_18 (nand_18_out, nand_11_out, nand_11_out);
  nand nand_19 (nand_19_out, nand_12_out, nand_12_out);
  nand nand_20 (nand_20_out, nand_13_out, nand_13_out);
  nand nand_21 (nand_21_out, nand_2_out, nand_2_out);
  nand nand_22 (nand_22_out, nand_3_out, nand_3_out);
  nand nand_23 (nand_23_out, nand_4_out, nand_4_out);
  nand nand_24 (nand_24_out, nand_5_out, nand_5_out);
  nand nand_25 (nand_25_out, nand_6_out, nand_6_out);
  nand nand_26 (nand_26_out, nand_7_out, nand_7_out);
  nand nand_27 (nand_27_out, nand_14_out, nand_14_out);
  nand nand_28 (nand_28_out, nand_16_out, nand_16_out);
  nand nand_29 (nand_29_out, nand_18_out, nand_18_out);
  nand nand_30 (nand_30_out, nand_19_out, nand_19_out);
  nand nand_31 (nand_31_out, nand_20_out, nand_20_out);
  nand nand_32 (nand_32_out, A, A);
  nand nand_33 (nand_33_out, not_3_out, not_3_out);
  nand nand_34 (nand_34_out, nand_9_out, nand_9_out);
  nand nand_35 (nand_35_out, nand_17_out, nand_17_out);
  nand nand_36 (nand_36_out, nand_21_out, nand_21_out);
  nand nand_37 (nand_37_out, nand_22_out, nand_22_out);
  nand nand_38 (nand_38_out, nand_23_out, nand_23_out);
  nand nand_39 (nand_39_out, nand_24_out, nand_24_out);
  nand nand_40 (nand_40_out, nand_25_out, nand_25_out);
  nand nand_41 (nand_41_out, nand_26_out, nand_26_out);
  nand nand_42 (nand_42_out, nand_27_out, nand_27_out);
  nand nand_43 (nand_43_out, nand_15_out, nand_15_out);
  nand nand_44 (nand_44_out, B, B);
  nand nand_45 (nand_45_out, nand_28_out, nand_28_out);
  nand nand_46 (out_5, nand_29_out, nand_30_out, nand_31_out);
  nand nand_47 (out_6, nand_32_out, nand_33_out);
  nand nand_48 (out_7, nand_36_out, nand_37_out, nand_38_out);
  nand nand_49 (out_8, nand_39_out, nand_40_out, nand_41_out);
  nand nand_50 (out_9, nand_42_out, nand_43_out);
  nand nand_51 (out_10, nand_44_out, nand_45_out);
  nand nand_52 (out_4, nand_34_out, nand_35_out);
endmodule

module \final  (
  input  in_1
);

  wire button_1_out, clock_1_out, n7_segment_universal_1_out_4, n7_segment_universal_1_out_5,
       n7_segment_universal_1_out_6, n7_segment_universal_1_out_7, n7_segment_universal_1_out_8,
       n7_segment_universal_1_out_9, n7_segment_universal_1_out_10, p1_1_out_4, p1_1_out_5, p1_1_out_6;

  Clock clock_1 (.out(clock_1_out));
  Button button_1 (.out(button_1_out));
  p1 p1_1 (
    .in_1(in_1), .out_4(p1_1_out_4), .out_5(p1_1_out_5), .out_6(p1_1_out_6), .in_2(button_1_out),
    .in_3(clock_1_out));
  _7_Segment_Universal u_7_segment_universal_1 (
    .out_4(n7_segment_universal_1_out_4), .out_5(n7_segment_universal_1_out_5),
    .out_6(n7_segment_universal_1_out_6), .out_7(n7_segment_universal_1_out_7),
    .out_8(n7_segment_universal_1_out_8), .out_9(n7_segment_universal_1_out_9),
    .out_10(n7_segment_universal_1_out_10), .A(p1_1_out_4), .B(p1_1_out_5), .C(p1_1_out_6));
  _7_Segment_Display u_7_segment_display_1 (
    .g(n7_segment_universal_1_out_10), .f(n7_segment_universal_1_out_9), .a(n7_segment_universal_1_out_4),
    .b(n7_segment_universal_1_out_5), .e(n7_segment_universal_1_out_8), .d(n7_segment_universal_1_out_7),
    .c(n7_segment_universal_1_out_6));  // open: dp
endmodule
